# Fritzing sketch hub (saved by Fritzing 0.9.2b)
breadboards: 1

parts:
  nRF24L01 = nRF24L01
  C3 = Electrolytic Capacitor [capacitance=1µF package="100 mil [THT, electrolytic]"]
  R9 = Resistor [tolerance=±5% resistance=220 package=THT]
  LED1 = LED - 5mm [color="Blue (470nm)" package="5 mm [THT]"]
  MCU = Arduino Micro (Rev3)

nets:
  VCC: nRF24L01.VCC, C3.+, MCU.3V3
  N1: nRF24L01.CSN, MCU.D10_PWM/A10
  N2: nRF24L01.MOSI, MCU.D11_PWM
  N3: nRF24L01.IRQ, MCU.D3/SCL
  GND: nRF24L01.GND, C3.-, R9.Pin_1, MCU.GND
  N4: nRF24L01.CE, MCU.D9_PWM/A9
  N5: nRF24L01.SCK, MCU.D13_PWM
  N6: nRF24L01.MISO, MCU.D12_PWM/A11
  N7: R9.Pin_0, LED1.cathode
  N8: LED1.anode, MCU.D7

custom parts:
  nRF24L01: nRF24L01 module
